# Fritzing sketch bonus4 (saved by Fritzing 0.9.2b)
breadboards: 1

parts:
  S1 = Pushbutton [package="[THT]"]
  J1 = T Cobbler Plus
  LED1 = LED - 5mm [color="Green (555nm)" package="5 mm [THT]"]
  R1 = Resistor [tolerance=±5% resistance=56 package=THT]
  LED2 = LED - 5mm [color="Yellow (592nm)" package="5 mm [THT]"]
  R2 = Resistor [tolerance=±5% resistance=56 package=THT]
  LED3 = LED - 5mm [color="Red (633nm)" package="5 mm [THT]"]
  R3 = Resistor [tolerance=±5% resistance=56 package=THT]
  R4 = Resistor [tolerance=±5% resistance=4.7k package=THT]
  LED4 = LED - 5mm [color="Red (633nm)" package="5 mm [THT]"]
  R5 = Resistor [tolerance=±5% resistance=56 package=THT]
  LED5 = LED - 5mm [color="Green (555nm)" package="5 mm [THT]"]
  R6 = Resistor [tolerance=±5% resistance=56 package=THT]
  LED6 = LED - 5mm [color="Yellow (595nm)" package="5 mm [THT]"]
  R7 = Resistor [tolerance=±5% resistance=56 package=THT]
  PIR1 = PIR sensor  # not connected

nets:
  N1: S1.Pin_1, S1.Pin_2, J1.3V3
  N2: S1.Pin_3, S1.Pin_4, J1.#4, R4.Pin_0
  N3: J1.SCL, R1.Pin_0, R2.Pin_0, R3.Pin_0
  N4: J1.#22, LED1.anode
  N5: J1.#23, LED2.anode
  N6: J1.3.3V, LED3.anode
  N7: J1.EEC, LED6.anode
  N8: J1.GND#29, R5.Pin_0, R6.Pin_0, R7.Pin_0
  N9: J1.#20, LED4.anode, R5.Pin_1
  N10: J1.GND#38, LED5.anode
  N11: LED1.cathode, R1.Pin_1
  N12: LED2.cathode, R2.Pin_1
  N13: LED3.cathode, R3.Pin_1
  N14: LED5.cathode, R6.Pin_1
  N15: LED6.cathode, R7.Pin_1

custom parts:
  T Cobbler Plus: The T-Cobbler Plus is an add on prototyping board from Adafruit specifically designed for the Raspberry Pi B+ that can break out all those tasty power, GPIO, I2C and SPI pins from the 40-pin header onto a solderless breadboard. This set will make "cobbling together" prototypes with the Pi super easy. The T-Cobbler Plus can plug into any solderless breadboard.
