# Fritzing sketch t4 (saved by Fritzing 0.9.2b)
breadboards: 1

parts:
  S1 = Pushbutton [package="[THT]"]
  J1 = T Cobbler Plus
  LED1 = LED - 5mm [color="Green (555nm)" package="5 mm [THT]"]
  R1 = Resistor [tolerance=±5% resistance=56 package=THT]
  R4 = Resistor [tolerance=±5% resistance=4.7k package=THT]
  PIR1 = PIR sensor  # not connected

nets:
  N1: S1.Pin_1, S1.Pin_2, J1.3V3
  N2: S1.Pin_3, S1.Pin_4, J1.#4, R4.Pin_0
  N3: J1.SCL, R1.Pin_0
  N4: J1.#22, LED1.anode
  N5: LED1.cathode, R1.Pin_1

custom parts:
  T Cobbler Plus: The T-Cobbler Plus is an add on prototyping board from Adafruit specifically designed for the Raspberry Pi B+ that can break out all those tasty power, GPIO, I2C and SPI pins from the 40-pin header onto a solderless breadboard. This set will make "cobbling together" prototypes with the Pi super easy. The T-Cobbler Plus can plug into any solderless breadboard.
